// Logisim project Project4Given.circ as structural Verilog: 9 circuits, main circuit NIC
module main (
  input  En_Noise
);

  wire CLK, keyboard_1_avail, multiplexer_1_out, nic_1_int, nic_1_tx, noisychannel_1_out,
       terminalcontroller_1_cs, terminalcontroller_1_kben, terminalcontroller_1_o,
       terminalcontroller_1_ttyen, terminalcontroller_1_w;
  wire [1:0] terminalcontroller_1_addr;
  wire [6:0] keyboard_1_data, terminalcontroller_1_ttydata;
  wire [7:0] nic_1_dataout, terminalcontroller_1_dataout, terminalcontroller_1_status;

  TTY tty_1 (.data(terminalcontroller_1_ttydata), .clk(CLK), .we(terminalcontroller_1_ttyen));  // open: clr
  Keyboard keyboard_1 (
    .clk(CLK), .re(terminalcontroller_1_kben), .avail(keyboard_1_avail), .data(keyboard_1_data));  // open: clr
  LED DR (.in(terminalcontroller_1_status[1]));
  LED TBNF (.in(terminalcontroller_1_status[2]));
  LED TXI (.in(terminalcontroller_1_status[3]));
  LED NF (.in(terminalcontroller_1_status[4]));
  LED OR (.in(terminalcontroller_1_status[5]));
  LED SDE (.in(terminalcontroller_1_status[6]));
  LED FE (.in(terminalcontroller_1_status[7]));
  Clock clock_1 (.out(CLK));
  TerminalController terminalcontroller_1 (
    .TTYEN(terminalcontroller_1_ttyen), .TTYDATA(terminalcontroller_1_ttydata),
    .STATUS(terminalcontroller_1_status), .KBEN(terminalcontroller_1_kben), .KBRDY(keyboard_1_avail),
    .KBDATA(keyboard_1_data), .CLK(CLK), .DIV(4'b0011), .INT(nic_1_int), .CS(terminalcontroller_1_cs),
    .O(terminalcontroller_1_o), .W(terminalcontroller_1_w), .ADDR(terminalcontroller_1_addr),
    .DATAOUT(terminalcontroller_1_dataout), .DATAIN(nic_1_dataout));
  NIC nic_1 (
    .INT(nic_1_int), .CS(terminalcontroller_1_cs), .O(terminalcontroller_1_o), .W(terminalcontroller_1_w),
    .ADDR(terminalcontroller_1_addr), .DATAIN(terminalcontroller_1_dataout), .DATAOUT(nic_1_dataout),
    .CLK(CLK), .TX(nic_1_tx), .RX(multiplexer_1_out));
  Shift_Register #(.length(32)) shift_register_1 (
    .in(nic_1_tx), .clk(CLK));  // open: shift, out, load, clr, d0, q0, d1, q1, d2, q2, d3, q3, d4, q4, d5, q5, d6, q6, d7, q7, d8, q8, d9, q9, d10, q10, d11, q11, d12, q12, d13, q13, d14, q14, d15, q15, d16, q16, d17, q17, d18, q18, d19, q19, d20, q20, d21, q21, d22, q22, d23, q23, d24, q24, d25, q25, d26, q26, d27, q27, d28, q28, d29, q29, d30, q30, d31, q31
  Shift_Register #(.length(32)) shift_register_2 (
    .in(multiplexer_1_out), .clk(CLK));  // open: shift, out, load, clr, d0, q0, d1, q1, d2, q2, d3, q3, d4, q4, d5, q5, d6, q6, d7, q7, d8, q8, d9, q9, d10, q10, d11, q11, d12, q12, d13, q13, d14, q14, d15, q15, d16, q16, d17, q17, d18, q18, d19, q19, d20, q20, d21, q21, d22, q22, d23, q23, d24, q24, d25, q25, d26, q26, d27, q27, d28, q28, d29, q29, d30, q30, d31, q31
  NoisyChannel noisychannel_1 (.In(nic_1_tx), .Rate(16'h800), .CLK(CLK), .Out(noisychannel_1_out));
  Multiplexer #(.enable("false")) multiplexer_1 (
    .in0(nic_1_tx), .in1(noisychannel_1_out), .out(multiplexer_1_out), .sel(En_Noise));

  // Notes on the sheet:
  //   Div
  //   Noise Rate
endmodule

module TerminalController (
  input  KBRDY,
  input  [6:0] KBDATA,
  input  INT,
  input  [7:0] DATAIN,
  input  CLK,
  input  [3:0] DIV,
  output KBEN,
  output CS,
  output O,
  output TTYEN,
  output W,
  output [6:0] TTYDATA,
  output [1:0] ADDR,
  output [7:0] STATUS,
  output [7:0] DATAOUT
);

  wire DOCHECKS, JMP, not_4_out, not_5_out, not_6_out, STATUSEN, TF, TTYDATAOUTSEL, TTYENP;
  wire [1:0] and_2_out, DATAOUTSEL;
  wire [7:0] DATABUSBYTE, INST, JUMPTARGET, multiplexer_1_out, multiplexer_3_out;
  wire [7:7] multiplexer_2_out;
  wire [23:11] rom_1_data;

  ROM #(.dataWidth(24)) rom_1 (
    .addr(INST),
    .data({rom_1_data[23:21], ADDR, KBEN, TTYENP, DATAOUTSEL, TTYDATAOUTSEL, rom_1_data[13:11], DOCHECKS, STATUSEN, JMP, DATABUSBYTE}),
    .sel(1'b1));
  not not_1 (W, rom_1_data[21]);
  not not_2 (O, rom_1_data[22]);
  not not_3 (CS, rom_1_data[23]);
  Multiplexer #(.select(2), .width(8), .enable("false")) multiplexer_1 (
    .in0({4'b0000, DIV}), .in1(DATABUSBYTE), .in2({1'b1, KBDATA}), .in3({8{1'b0}}), .out(multiplexer_1_out),
    .sel(DATAOUTSEL));
  assign DATAOUT = not_4_out ? multiplexer_1_out : 8'bz;  // Controlled_Buffer controlled_buffer_1
  not not_4 (not_4_out, W);
  Multiplexer #(.width(8), .enable("false")) multiplexer_2 (
    .in0(DATAIN), .in1(DATABUSBYTE), .out({multiplexer_2_out[7], TTYDATA}), .sel(TTYDATAOUTSEL));
  and and_1 (TTYEN, multiplexer_2_out[7], TTYENP);
  Counter counter_1 (.load(JMP), .D(JUMPTARGET), .count(not_5_out), .Q(INST), .clk(CLK));  // open: carry, clr
  not not_5 (not_5_out, JMP);
  Multiplexer #(.width(8), .enable("false")) multiplexer_3 (
    .in0(8'h20), .in1(8'h30), .out(multiplexer_3_out), .sel(TF));
  and and_2 (and_2_out[0], KBRDY, DOCHECKS);
  and and_3 (and_2_out[1], DOCHECKS, not_6_out);
  not not_6 (not_6_out, INT);
  Comparator #(.width(7), .mode("unsigned")) comparator_1 (.a(KBDATA), .b(7'b0001010), .eq(TF));  // open: gt, lt
  Register register_1 (.D(DATAIN), .en(STATUSEN), .Q(STATUS), .clk(CLK));  // open: clr
  Multiplexer #(.select(2), .width(8), .enable("false")) multiplexer_4 (
    .in0(DATABUSBYTE), .in1(multiplexer_3_out), .in2(8'h10), .in3(8'h10), .out(JUMPTARGET), .sel(and_2_out));

  // Other names for the same wires on the sheet: KBDATABUSBYTE[6:0] = KBDATA

  // Notes on the sheet:
  //   contents of rom_1 (hex, n*v repeats v):
  //   0 b80000 b80000 0 a88002 a88002 0 a08001 a08001 0 c00000 c00000 c00200 509 0 0 d00000 d00000 d20000
  //   109 12*0 b10000 b10000 b10000 40000 109 11*0 b10000 b10000 b10000 40000 a08003 a08003 109
endmodule

module NIC (
  input  CS,
  input  O,
  input  W,
  input  RX,
  input  [1:0] ADDR,
  input  [7:0] DATAIN,
  input  CLK,
  output INT,
  output TX,
  output [7:0] DATAOUT
);

  ClockDivisor clockdivisor_1 ();  // open: in_2, Output, in_1
endmodule

module NoisyChannel (
  input  [15:0] Rate,
  input  In,
  input  CLK,
  output Out
);

  wire Flip;
  wire [15:0] RNG;
  wire [31:0] adder_1_out, multiplier_1_out, SEED;

  xor xor_1 (Out, In, Flip);
  Multiplier #(.width(32)) multiplier_1 (.a(SEED), .b(32'h15a4e35), .out(multiplier_1_out));  // open: cin, cout
  Adder #(.width(32)) adder_1 (.a(multiplier_1_out), .b(32'h1), .out(adder_1_out));  // open: cin, cout
  Comparator #(.width(16), .mode("unsigned")) comparator_1 (.a(RNG), .b(Rate), .lt(Flip));  // open: gt, eq
  Register #(.width(32)) register_1 (.D(adder_1_out), .Q(SEED), .clk(CLK));  // open: en, clr
  assign RNG = SEED[15:0] ^ SEED[31:16];  // XOR_Gate xor_2, 16 bits wide
endmodule

module ClockDivisor (
  input  [3:0] in_1,
  input  in_2,
  output Output
);

  wire CLK, Val3, Val4, Val5, Val6, Val7, Val8, Val9, Val10, Val11, Val12, Val13, Val14, Val15;
  wire [12:0] bit_extender_1_out;

  Clock clock_1 (.out(CLK));
  Counter #(.width(4), .max('h3), .ongoal("load")) counter_1 (
    .D(4'b0001), .carry(Val3), .clk(CLK), .clr(bit_extender_1_out[12]));  // open: load, count, Q
  Counter #(.width(4), .max('h4), .ongoal("load")) counter_2 (
    .D(4'b0001), .carry(Val4), .clk(CLK), .clr(bit_extender_1_out[11]));  // open: load, count, Q
  Counter #(.width(4), .max('h6), .ongoal("load")) counter_3 (
    .D(4'b0001), .carry(Val6), .clk(CLK), .clr(bit_extender_1_out[9]));  // open: load, count, Q
  Counter #(.width(4), .max('h5), .ongoal("load")) counter_4 (
    .D(4'b0001), .carry(Val5), .clk(CLK), .clr(bit_extender_1_out[10]));  // open: load, count, Q
  Counter #(.width(4), .max('h7), .ongoal("load")) counter_5 (
    .D(4'b0001), .carry(Val7), .clk(CLK), .clr(bit_extender_1_out[8]));  // open: load, count, Q
  Counter #(.width(4), .max('h8), .ongoal("load")) counter_6 (
    .D(4'b0001), .carry(Val8), .clk(CLK), .clr(bit_extender_1_out[7]));  // open: load, count, Q
  Multiplexer #(.select(4)) multiplexer_1 (
    .in3(Val3), .in4(Val4), .in5(Val5), .in6(Val6), .in7(Val7), .in8(Val8), .in9(Val9), .in10(Val10),
    .in11(Val11), .in12(Val12), .in13(Val13), .in14(Val14), .in15(Val15), .out(Output), .sel(in_1));  // open: in0, in1, in2, en
  Counter #(.width(4), .max('ha), .ongoal("load")) counter_7 (
    .D(4'b0001), .carry(Val10), .clk(CLK), .clr(bit_extender_1_out[5]));  // open: load, count, Q
  Counter #(.width(4), .max('h9), .ongoal("load")) counter_8 (
    .D(4'b0001), .carry(Val9), .clk(CLK), .clr(bit_extender_1_out[6]));  // open: load, count, Q
  assign bit_extender_1_out = {{12{in_2}}, in_2};  // Bit_Extender bit_extender_1
  Counter #(.width(4), .max('hb), .ongoal("load")) counter_9 (
    .D(4'b0001), .carry(Val11), .clk(CLK), .clr(bit_extender_1_out[4]));  // open: load, count, Q
  Counter #(.width(4), .max('hc), .ongoal("load")) counter_10 (
    .D(4'b0001), .carry(Val12), .clk(CLK), .clr(bit_extender_1_out[3]));  // open: load, count, Q
  Counter #(.width(4), .max('he), .ongoal("load")) counter_11 (
    .D(4'b0001), .carry(Val14), .clk(CLK), .clr(bit_extender_1_out[1]));  // open: load, count, Q
  Counter #(.width(4), .max('hd), .ongoal("load")) counter_12 (
    .D(4'b0001), .carry(Val13), .clk(CLK), .clr(bit_extender_1_out[2]));  // open: load, count, Q
  Counter #(.width(4), .max('hf), .ongoal("load")) counter_13 (
    .D(4'b0001), .carry(Val15), .clk(CLK), .clr(bit_extender_1_out[0]));  // open: load, count, Q

  // Other names for the same wires on the sheet: Input[3:0] = in_1
endmodule

module BitStuffer (
  input  in_1,
  input  in_2,
  input  in_3,
  input  [21:0] in_4
);

  wire controlled_buffer_1_out, controlled_buffer_2_out, counter_1_carry, counter_2_carry, d_ff_1_q,
       d_ff_2_q, d_ff_3_q, DisableSh, not_1_out, not_2_out, not_3_out, not_4_out, not_5_out, or_1_out,
       or_2_out, shift_register_1_out;
  wire [1:0] controlled_buffer_3_out;

  not not_1 (not_1_out, DisableSh);
  assign controlled_buffer_1_out = in_1 ? not_1_out : 1'bz;  // Controlled_Buffer controlled_buffer_1
  Shift_Register shift_register_1 (
    .shift(controlled_buffer_1_out), .in(in_3), .clk(in_2), .out(shift_register_1_out));  // open: load, clr, d0, q0, d1, q1, d2, q2, d3, q3, d4, q4, d5, q5, d6, q6, d7, q7
  D_Flip_Flop d_ff_1 (.clk(in_2), .D(shift_register_1_out), .Q(d_ff_1_q));  // open: Qn, preset, en, reset
  not not_2 (not_2_out, d_ff_1_q);
  Counter #(.width(3), .max('h4)) counter_1 (
    .count(d_ff_1_q), .carry(counter_1_carry), .clk(in_2), .clr(or_1_out));  // open: load, D, Q
  or or_1 (or_1_out, d_ff_2_q, not_3_out);
  not not_3 (not_3_out, d_ff_1_q);
  D_Flip_Flop d_ff_2 (.clk(in_2), .D(counter_1_carry), .Q(d_ff_2_q));  // open: Qn, preset, en, reset
  not not_4 (not_4_out, counter_1_carry);
  Counter #(.width(3), .max('h4)) counter_2 (
    .count(not_2_out), .carry(counter_2_carry), .clk(in_2), .clr(or_2_out));  // open: load, D, Q
  or or_2 (or_2_out, d_ff_1_q, d_ff_3_q);
  or or_3 (DisableSh, counter_1_carry, counter_2_carry);
  assign controlled_buffer_2_out = not_5_out ? shift_register_1_out : 1'bz;  // Controlled_Buffer controlled_buffer_2
  D_Flip_Flop d_ff_3 (.clk(in_2), .D(counter_2_carry), .Q(d_ff_3_q));  // open: Qn, preset, en, reset
  assign controlled_buffer_3_out[0] = in_1 ? counter_2_carry : 1'bz;  // Controlled_Buffer controlled_buffer_3
  assign controlled_buffer_3_out[1] = in_1 ? counter_1_carry : 1'bz;  // Controlled_Buffer controlled_buffer_4
  not not_5 (not_5_out, in_1);
  Shift_Register shift_register_2 (
    .in(controlled_buffer_2_out), .clk(in_2));  // open: shift, out, load, clr, d0, q0, d1, q1, d2, q2, d3, q3, d4, q4, d5, q5, d6, q6, d7, q7
  Multiplexer #(.select(2)) multiplexer_1 (
    .in0(shift_register_1_out), .in1(counter_2_carry), .in2(not_4_out), .out(controlled_buffer_2_out),
    .sel(controlled_buffer_3_out));  // open: in3, en

  // Other names for the same wires on the sheet: CLK = in_2; DataW = in_1; Input = in_3; Raw[21:0] = in_4
endmodule

module FIFO22 (
  input  [21:0] in_1,
  input  [21:0] in_2,
  input  [21:0] in_3,
  input  [21:0] in_4,
  input  [21:0] in_5,
  input  [21:0] in_6,
  input  [21:0] in_7,
  input  [21:0] in_8,
  input  [21:0] in_9,
  input  [21:0] in_10,
  input  [21:0] in_11,
  input  [21:0] in_12,
  input  [21:0] in_13,
  input  [21:0] in_14,
  input  [21:0] in_15,
  input  [21:0] in_16,
  input  in_17,
  input  in_18,
  input  in_19,
  input  [21:0] in_20,
  output [21:0] out_21,
  output [21:0] out_22,
  output [21:0] out_23,
  output [21:0] out_24,
  output [21:0] out_25,
  output [21:0] out_26,
  output [21:0] out_27,
  output [21:0] out_28,
  output [21:0] out_29,
  output [21:0] out_30,
  output [21:0] out_31,
  output [21:0] out_32,
  output [21:0] out_33,
  output [21:0] out_34,
  output [21:0] out_35,
  output [21:0] out_36,
  output [21:0] out_37
);

  wire CLK;
  wire [21:0] multiplexer_1_out, multiplexer_2_out, multiplexer_3_out, multiplexer_4_out, multiplexer_5_out,
       multiplexer_6_out, multiplexer_7_out, multiplexer_8_out, multiplexer_9_out, multiplexer_10_out,
       multiplexer_11_out, multiplexer_12_out, multiplexer_13_out, multiplexer_14_out, multiplexer_15_out,
       multiplexer_16_out, register_1_q, register_2_q, register_3_q, register_4_q, register_5_q,
       register_6_q, register_7_q, register_8_q, register_9_q, register_10_q, register_11_q, register_12_q,
       register_13_q, register_14_q, register_15_q;

  Multiplexer #(.width(22)) multiplexer_1 (.in0(in_20), .in1(in_1), .out(multiplexer_1_out), .sel(in_17));  // open: en
  Register #(.width(22)) register_1 (.D(multiplexer_1_out), .en(in_18), .Q(register_1_q), .clk(CLK));  // open: clr
  assign out_22 = in_19 ? register_1_q : 22'bz;  // Controlled_Buffer controlled_buffer_1
  Clock clock_1 (.out(CLK));
  Multiplexer #(.width(22)) multiplexer_2 (
    .in0(register_1_q), .in1(in_2), .out(multiplexer_2_out), .sel(in_17));  // open: en
  Register #(.width(22)) register_2 (.D(multiplexer_2_out), .en(in_18), .Q(register_2_q), .clk(CLK));  // open: clr
  assign out_23 = in_19 ? register_2_q : 22'bz;  // Controlled_Buffer controlled_buffer_2
  Multiplexer #(.width(22)) multiplexer_3 (
    .in0(register_2_q), .in1(in_3), .out(multiplexer_3_out), .sel(in_17));  // open: en
  Register #(.width(22)) register_3 (.D(multiplexer_3_out), .en(in_18), .Q(register_3_q), .clk(CLK));  // open: clr
  assign out_24 = in_19 ? register_3_q : 22'bz;  // Controlled_Buffer controlled_buffer_3
  Multiplexer #(.width(22)) multiplexer_4 (
    .in0(register_3_q), .in1(in_4), .out(multiplexer_4_out), .sel(in_17));  // open: en
  Multiplexer #(.width(22)) multiplexer_5 (
    .in0(register_4_q), .in1(in_5), .out(multiplexer_5_out), .sel(in_17));  // open: en
  Register #(.width(22)) register_4 (.D(multiplexer_4_out), .en(in_18), .Q(register_4_q), .clk(CLK));  // open: clr
  assign out_25 = in_19 ? register_4_q : 22'bz;  // Controlled_Buffer controlled_buffer_4
  Register #(.width(22)) register_5 (.D(multiplexer_5_out), .en(in_18), .Q(register_5_q), .clk(CLK));  // open: clr
  assign out_26 = in_19 ? register_5_q : 22'bz;  // Controlled_Buffer controlled_buffer_5
  Multiplexer #(.width(22)) multiplexer_6 (
    .in0(register_5_q), .in1(in_6), .out(multiplexer_6_out), .sel(in_17));  // open: en
  Register #(.width(22)) register_6 (.D(multiplexer_6_out), .en(in_18), .Q(register_6_q), .clk(CLK));  // open: clr
  assign out_27 = in_19 ? register_6_q : 22'bz;  // Controlled_Buffer controlled_buffer_6
  Register #(.width(22)) register_7 (.D(multiplexer_7_out), .en(in_18), .Q(register_7_q), .clk(CLK));  // open: clr
  Multiplexer #(.width(22)) multiplexer_7 (
    .in0(register_6_q), .in1(in_7), .out(multiplexer_7_out), .sel(in_17));  // open: en
  assign out_28 = in_19 ? register_7_q : 22'bz;  // Controlled_Buffer controlled_buffer_7
  Multiplexer #(.width(22)) multiplexer_8 (
    .in0(register_7_q), .in1(in_8), .out(multiplexer_8_out), .sel(in_17));  // open: en
  Register #(.width(22)) register_8 (.D(multiplexer_8_out), .en(in_18), .Q(register_8_q), .clk(CLK));  // open: clr
  Multiplexer #(.width(22)) multiplexer_9 (
    .in0(register_8_q), .in1(in_9), .out(multiplexer_9_out), .sel(in_17));  // open: en
  assign out_29 = in_19 ? register_8_q : 22'bz;  // Controlled_Buffer controlled_buffer_8
  Register #(.width(22)) register_9 (.D(multiplexer_9_out), .en(in_18), .Q(register_9_q), .clk(CLK));  // open: clr
  assign out_30 = in_19 ? register_9_q : 22'bz;  // Controlled_Buffer controlled_buffer_9
  Register #(.width(22)) register_10 (.D(multiplexer_10_out), .en(in_18), .Q(register_10_q), .clk(CLK));  // open: clr
  Multiplexer #(.width(22)) multiplexer_10 (
    .in0(register_9_q), .in1(in_10), .out(multiplexer_10_out), .sel(in_17));  // open: en
  assign out_31 = in_19 ? register_10_q : 22'bz;  // Controlled_Buffer controlled_buffer_10
  Multiplexer #(.width(22)) multiplexer_11 (
    .in0(register_10_q), .in1(in_11), .out(multiplexer_11_out), .sel(in_17));  // open: en
  Register #(.width(22)) register_11 (.D(multiplexer_11_out), .en(in_18), .Q(register_11_q), .clk(CLK));  // open: clr
  assign out_32 = in_19 ? register_11_q : 22'bz;  // Controlled_Buffer controlled_buffer_11
  Multiplexer #(.width(22)) multiplexer_12 (
    .in0(register_11_q), .in1(in_12), .out(multiplexer_12_out), .sel(in_17));  // open: en
  Register #(.width(22)) register_12 (.D(multiplexer_12_out), .en(in_18), .Q(register_12_q), .clk(CLK));  // open: clr
  Multiplexer #(.width(22)) multiplexer_13 (
    .in0(register_12_q), .in1(in_13), .out(multiplexer_13_out), .sel(in_17));  // open: en
  assign out_33 = in_19 ? register_12_q : 22'bz;  // Controlled_Buffer controlled_buffer_12
  Register #(.width(22)) register_13 (.D(multiplexer_13_out), .en(in_18), .Q(register_13_q), .clk(CLK));  // open: clr
  assign out_34 = in_19 ? register_13_q : 22'bz;  // Controlled_Buffer controlled_buffer_13
  Multiplexer #(.width(22)) multiplexer_14 (
    .in0(register_13_q), .in1(in_14), .out(multiplexer_14_out), .sel(in_17));  // open: en
  Register #(.width(22)) register_14 (.D(multiplexer_14_out), .en(in_18), .Q(register_14_q), .clk(CLK));  // open: clr
  assign out_35 = in_19 ? register_14_q : 22'bz;  // Controlled_Buffer controlled_buffer_14
  Register #(.width(22)) register_15 (.D(multiplexer_15_out), .en(in_18), .Q(register_15_q), .clk(CLK));  // open: clr
  Multiplexer #(.width(22)) multiplexer_15 (
    .in0(register_14_q), .in1(in_15), .out(multiplexer_15_out), .sel(in_17));  // open: en
  assign out_36 = in_19 ? register_15_q : 22'bz;  // Controlled_Buffer controlled_buffer_15
  Multiplexer #(.width(22)) multiplexer_16 (
    .in0(register_15_q), .in1(in_16), .out(multiplexer_16_out), .sel(in_17));  // open: en
  Register #(.width(22)) register_16 (.D(multiplexer_16_out), .en(in_18), .Q(out_21), .clk(CLK));  // open: clr
  assign out_37 = in_19 ? out_21 : 22'bz;  // Controlled_Buffer controlled_buffer_16
endmodule

module SECDED (
  input  [15:0] Input,
  output [21:0] Output,
  output P1,
  output P2,
  output P4,
  output P8,
  output P16,
  output P0
);

  wire xor_1_out, xor_2_out, xor_3_out, xor_4_out, xor_5_out, xor_6_out, xor_7_out, xor_8_out, xor_9_out,
       xor_10_out, xor_11_out, xor_12_out, xor_13_out, xor_14_out, xor_15_out, xor_16_out, xor_17_out,
       xor_18_out, xor_19_out, xor_20_out, xor_21_out, xor_22_out, xor_23_out, xor_24_out, xor_25_out,
       xor_26_out, xor_27_out, xor_28_out, xor_29_out, xor_30_out, xor_31_out, xor_32_out, xor_33_out,
       xor_34_out, xor_35_out, xor_36_out, xor_37_out, xor_38_out, xor_39_out, xor_40_out, xor_41_out,
       xor_42_out, xor_43_out, xor_44_out, xor_45_out, xor_46_out, xor_47_out, xor_53_out, xor_54_out;

  xor xor_1 (xor_1_out, Output[1], Output[2]);
  xor xor_2 (xor_2_out, Output[4], Output[8]);
  xor xor_3 (xor_3_out, Input[0], Input[1]);
  xor xor_4 (xor_4_out, Input[3], Input[4]);
  xor xor_5 (xor_5_out, Input[6], Input[8]);
  xor xor_6 (xor_6_out, Input[10], Input[11]);
  xor xor_7 (xor_7_out, Input[13], Input[15]);
  xor xor_8 (xor_8_out, Input[0], Input[2]);
  xor xor_9 (xor_9_out, Input[3], Input[5]);
  xor xor_10 (xor_10_out, Input[6], Input[9]);
  xor xor_11 (xor_11_out, Input[10], Input[12]);
  xor xor_12 (xor_12_out, Input[1], Input[2]);
  xor xor_13 (xor_13_out, Input[3], Input[7]);
  xor xor_14 (xor_14_out, Input[8], Input[9]);
  xor xor_15 (xor_15_out, Input[10], Input[14]);
  xor xor_16 (xor_16_out, Input[4], Input[5]);
  xor xor_17 (xor_17_out, Input[6], Input[7]);
  xor xor_18 (xor_18_out, Input[8], Input[9]);
  xor xor_19 (xor_19_out, Input[11], Input[12]);
  xor xor_20 (xor_20_out, Input[13], Input[14]);
  xor xor_21 (xor_21_out, Input[0], Input[1]);
  xor xor_22 (xor_22_out, Input[2], Input[3]);
  xor xor_23 (xor_23_out, Input[4], Input[5]);
  xor xor_24 (xor_24_out, Input[6], Input[7]);
  xor xor_25 (xor_25_out, Input[8], Input[9]);
  xor xor_26 (xor_26_out, Input[10], Input[11]);
  xor xor_27 (xor_27_out, Input[12], Input[13]);
  xor xor_28 (xor_28_out, Input[14], Input[15]);
  xor xor_29 (xor_29_out, xor_1_out, xor_2_out);
  xor xor_30 (xor_30_out, xor_3_out, xor_4_out);
  xor xor_31 (xor_31_out, xor_5_out, xor_6_out);
  xor xor_32 (xor_32_out, xor_8_out, xor_9_out);
  xor xor_33 (xor_33_out, xor_10_out, xor_11_out);
  xor xor_34 (xor_34_out, xor_12_out, xor_13_out);
  xor xor_35 (xor_35_out, xor_14_out, xor_15_out);
  xor xor_36 (xor_36_out, xor_16_out, xor_17_out);
  xor xor_37 (xor_37_out, xor_18_out, Input[10]);
  xor xor_38 (xor_38_out, xor_19_out, xor_20_out);
  xor xor_39 (xor_39_out, xor_21_out, xor_22_out);
  xor xor_40 (xor_40_out, xor_23_out, xor_24_out);
  xor xor_41 (xor_41_out, xor_26_out, xor_27_out);
  xor xor_42 (xor_42_out, xor_33_out, Input[13]);
  xor xor_43 (xor_43_out, xor_35_out, Input[15]);
  xor xor_44 (xor_44_out, xor_40_out, xor_25_out);
  xor xor_45 (xor_45_out, xor_41_out, xor_28_out);
  xor xor_46 (xor_46_out, xor_29_out, Output[16]);
  xor xor_47 (xor_47_out, xor_31_out, xor_7_out);
  xor xor_48 (Output[1], xor_30_out, xor_47_out);
  xor xor_49 (Output[2], xor_32_out, xor_42_out);
  xor xor_50 (Output[4], xor_34_out, xor_43_out);
  xor xor_51 (Output[8], xor_36_out, xor_37_out);
  xor xor_52 (Output[16], xor_38_out, Input[15]);
  xor xor_53 (xor_53_out, xor_39_out, xor_44_out);
  xor xor_54 (xor_54_out, xor_53_out, xor_45_out);
  xor xor_55 (Output[0], xor_54_out, xor_46_out);

  assign {Output[21:17], Output[15:9], Output[7:5], Output[3]} = Input;
  assign P0 = Output[0];
  assign P1 = Output[1];
  assign P2 = Output[2];
  assign P4 = Output[4];
  assign P8 = Output[8];
  assign P16 = Output[16];

  // Other names for the same wires on the sheet: D0 = Input[0]; D1 = Input[1]; D2 = Input[2]; D3 = Input[3];
  //   D4 = Input[4]; D5 = Input[5]; D6 = Input[6]; D7 = Input[7]; D8 = Input[8]; D9 = Input[9]; D10 = Input[10];
  //   D11 = Input[11]; D12 = Input[12]; D13 = Input[13]; D14 = Input[14]; D15 = Input[15]
endmodule

module FIFO (
  input  in_1,
  input  in_2,
  input  in_3,
  input  in_4,
  input  in_5,
  input  in_6,
  input  in_7,
  input  in_8,
  input  in_9,
  input  in_10,
  input  in_11,
  input  in_12,
  input  in_13,
  input  in_14,
  input  in_15,
  input  in_16,
  input  in_17,
  input  in_18,
  input  in_19,
  input  in_20,
  input  in_21,
  output out_22,
  output out_23,
  output out_24,
  output out_25,
  output out_26,
  output out_27,
  output out_28,
  output out_29,
  output out_30,
  output out_31,
  output out_32,
  output out_33,
  output out_34,
  output out_35,
  output out_36,
  output out_37,
  output out_38
);

  wire multiplexer_1_out, multiplexer_2_out, multiplexer_3_out, multiplexer_4_out, multiplexer_5_out,
       multiplexer_6_out, multiplexer_7_out, multiplexer_8_out, multiplexer_9_out, multiplexer_10_out,
       multiplexer_11_out, multiplexer_12_out, multiplexer_13_out, multiplexer_14_out, multiplexer_15_out,
       multiplexer_16_out, register_1_q, register_2_q, register_3_q, register_4_q, register_5_q,
       register_6_q, register_7_q, register_8_q, register_9_q, register_10_q, register_11_q, register_12_q,
       register_13_q, register_14_q, register_15_q;

  Register #(.width(1)) register_1 (.D(multiplexer_1_out), .en(in_18), .Q(register_1_q), .clk(in_21));  // open: clr
  Multiplexer multiplexer_1 (.in0(in_20), .in1(in_1), .out(multiplexer_1_out), .sel(in_17));  // open: en
  assign out_23 = in_19 ? register_1_q : 1'bz;  // Controlled_Buffer controlled_buffer_1
  Register #(.width(1)) register_2 (.D(multiplexer_2_out), .en(in_18), .Q(register_2_q), .clk(in_21));  // open: clr
  Multiplexer multiplexer_2 (.in0(register_1_q), .in1(in_2), .out(multiplexer_2_out), .sel(in_17));  // open: en
  Multiplexer multiplexer_3 (.in0(register_2_q), .in1(in_3), .out(multiplexer_3_out), .sel(in_17));  // open: en
  assign out_24 = in_19 ? register_2_q : 1'bz;  // Controlled_Buffer controlled_buffer_2
  Register #(.width(1)) register_3 (.D(multiplexer_3_out), .en(in_18), .Q(register_3_q), .clk(in_21));  // open: clr
  Multiplexer multiplexer_4 (.in0(register_3_q), .in1(in_4), .out(multiplexer_4_out), .sel(in_17));  // open: en
  assign out_25 = in_19 ? register_3_q : 1'bz;  // Controlled_Buffer controlled_buffer_3
  Register #(.width(1)) register_4 (.D(multiplexer_4_out), .en(in_18), .Q(register_4_q), .clk(in_21));  // open: clr
  assign out_26 = in_19 ? register_4_q : 1'bz;  // Controlled_Buffer controlled_buffer_4
  Multiplexer multiplexer_5 (.in0(register_4_q), .in1(in_5), .out(multiplexer_5_out), .sel(in_17));  // open: en
  Register #(.width(1)) register_5 (.D(multiplexer_5_out), .en(in_18), .Q(register_5_q), .clk(in_21));  // open: clr
  assign out_27 = in_19 ? register_5_q : 1'bz;  // Controlled_Buffer controlled_buffer_5
  Register #(.width(1)) register_6 (.D(multiplexer_6_out), .en(in_18), .Q(register_6_q), .clk(in_21));  // open: clr
  Multiplexer multiplexer_6 (.in0(register_5_q), .in1(in_6), .out(multiplexer_6_out), .sel(in_17));  // open: en
  Multiplexer multiplexer_7 (.in0(register_6_q), .in1(in_7), .out(multiplexer_7_out), .sel(in_17));  // open: en
  assign out_28 = in_19 ? register_6_q : 1'bz;  // Controlled_Buffer controlled_buffer_6
  Multiplexer multiplexer_8 (.in0(register_7_q), .in1(in_8), .out(multiplexer_8_out), .sel(in_17));  // open: en
  Register #(.width(1)) register_7 (.D(multiplexer_7_out), .en(in_18), .Q(register_7_q), .clk(in_21));  // open: clr
  assign out_29 = in_19 ? register_7_q : 1'bz;  // Controlled_Buffer controlled_buffer_7
  Register #(.width(1)) register_8 (.D(multiplexer_8_out), .en(in_18), .Q(register_8_q), .clk(in_21));  // open: clr
  assign out_30 = in_19 ? register_8_q : 1'bz;  // Controlled_Buffer controlled_buffer_8
  Register #(.width(1)) register_9 (.D(multiplexer_9_out), .en(in_18), .Q(register_9_q), .clk(in_21));  // open: clr
  Multiplexer multiplexer_9 (.in0(register_8_q), .in1(in_9), .out(multiplexer_9_out), .sel(in_17));  // open: en
  assign out_31 = in_19 ? register_9_q : 1'bz;  // Controlled_Buffer controlled_buffer_9
  Multiplexer multiplexer_10 (.in0(register_9_q), .in1(in_10), .out(multiplexer_10_out), .sel(in_17));  // open: en
  Register #(.width(1)) register_10 (.D(multiplexer_10_out), .en(in_18), .Q(register_10_q), .clk(in_21));  // open: clr
  Multiplexer multiplexer_11 (.in0(register_10_q), .in1(in_11), .out(multiplexer_11_out), .sel(in_17));  // open: en
  assign out_32 = in_19 ? register_10_q : 1'bz;  // Controlled_Buffer controlled_buffer_10
  Register #(.width(1)) register_11 (.D(multiplexer_11_out), .en(in_18), .Q(register_11_q), .clk(in_21));  // open: clr
  Multiplexer multiplexer_12 (.in0(register_11_q), .in1(in_12), .out(multiplexer_12_out), .sel(in_17));  // open: en
  assign out_33 = in_19 ? register_11_q : 1'bz;  // Controlled_Buffer controlled_buffer_11
  Register #(.width(1)) register_12 (.D(multiplexer_12_out), .en(in_18), .Q(register_12_q), .clk(in_21));  // open: clr
  assign out_34 = in_19 ? register_12_q : 1'bz;  // Controlled_Buffer controlled_buffer_12
  Multiplexer multiplexer_13 (.in0(register_12_q), .in1(in_13), .out(multiplexer_13_out), .sel(in_17));  // open: en
  Register #(.width(1)) register_13 (.D(multiplexer_13_out), .en(in_18), .Q(register_13_q), .clk(in_21));  // open: clr
  assign out_35 = in_19 ? register_13_q : 1'bz;  // Controlled_Buffer controlled_buffer_13
  Multiplexer multiplexer_14 (.in0(register_13_q), .in1(in_14), .out(multiplexer_14_out), .sel(in_17));  // open: en
  Register #(.width(1)) register_14 (.D(multiplexer_14_out), .en(in_18), .Q(register_14_q), .clk(in_21));  // open: clr
  Multiplexer multiplexer_15 (.in0(register_14_q), .in1(in_15), .out(multiplexer_15_out), .sel(in_17));  // open: en
  assign out_36 = in_19 ? register_14_q : 1'bz;  // Controlled_Buffer controlled_buffer_14
  Multiplexer multiplexer_16 (.in0(register_15_q), .in1(in_16), .out(multiplexer_16_out), .sel(in_17));  // open: en
  Register #(.width(1)) register_15 (.en(in_18), .Q(register_15_q), .clk(in_21));  // open: D, clr
  assign out_37 = in_19 ? register_15_q : 1'bz;  // Controlled_Buffer controlled_buffer_15
  Register #(.width(1)) register_16 (.D(multiplexer_16_out), .en(in_18), .Q(out_22), .clk(in_21));  // open: clr
  assign out_38 = in_19 ? out_22 : 1'bz;  // Controlled_Buffer controlled_buffer_16

  // Other names for the same wires on the sheet: CLK = in_21
endmodule
